# Fritzing sketch CircuitoTeremim (saved by Fritzing 0.9.2b)

parts:
  Componente1 = Arduino Uno (Rev3)
  Componente2 = SRF05 Ultrasonic Rangefinder
  J1 = Piezo Speaker

nets:
  N1: Componente1.D12/MISO, J1.pin2
  GND: Componente1.GND, Componente2.GND, J1.pin1
  N2: Componente1.D5_PWM, Componente2.Echo
  N3: Componente1.D6_PWM, Componente2.Trig
  5V: Componente1.5V, Componente2.VCC

notes:
  6
  5
  12
